# Fritzing sketch btn0 (saved by Fritzing 0.9.4)
breadboards: 1

parts:
  R2 = Resistor [tolerance=±5% resistance=220 package=THT]
  LED1 = LED - 5mm [color="Red (633nm)" package="5 mm [THT]"]
  LED2 = LED - 5mm [color="Blue (470nm)" package="5 mm [THT]"]
  Arduino_Nano = Arduino Nano (Rev3.0)
  R4 = Resistor [tolerance=±5% resistance=10k package=THT]
  S8 = Round Pushbutton
  R7 = Resistor [tolerance=±5% resistance=220 package=THT]
  S9 = Round Pushbutton
  R3 = Resistor [tolerance=±5% resistance=10k package=THT]

nets:
  N1: R2.Pin_0, LED1.anode
  N2: R2.Pin_1, Arduino_Nano.D12/MISO
  N3: LED1.cathode, LED2.cathode, Arduino_Nano.GND, R4.Pin_0, S9.leg0
  N4: LED2.anode, R7.Pin_1
  N5: Arduino_Nano.D2, R4.Pin_1, S8.leg0
  N6: Arduino_Nano.D4, R7.Pin_0
  N7: Arduino_Nano.D10, S9.leg1, R3.Pin_0
  N8: Arduino_Nano.5V, S8.leg1, R3.Pin_1
