# Fritzing sketch led0 (saved by Fritzing 0.9.4)
circuit board: 3.84048cm x 5.70612cm
breadboards: 1

parts:
  Arduino_Nano = Arduino Nano (Rev3.0)
  LED1 = smd LED [color="Red (633nm)" package="0805 [SMD]"]
  R1 = Resistor [tolerance=±5% resistance=220 package="0402 [SMD]"]

nets:
  N1: Arduino_Nano.GND, LED1.cathode
  N2: Arduino_Nano.D12/MISO, R1.Pin_1
  N3: LED1.anode, R1.Pin_0
