# Fritzing sketch 2board_communication (saved by Fritzing 0.9.4)

parts:
  UNO = Arduino Uno (Rev3)
  NANO = Arduino Nano (Rev3.0)

nets:
  GND: UNO.GND, NANO.GND
  N1: UNO.D0/RX, NANO.D1/TX
  N2: UNO.D1/TX, NANO.D0/RX
