# Fritzing sketch IR_sensor (saved by Fritzing 0.9.4)
breadboards: 1

parts:
  IR_transmitter = LED - 5mm [color="Infrared (850nm)" package="5 mm [THT]"]
  IR_receiver = LED - 5mm [color="Blue (430nm)" package="5 mm [THT]"]
  Arduino_Nano = Arduino Nano (Rev3.0)
  LED0 = LED - 5mm [color="Red (633nm)" package="5 mm [THT]"]
  R1 = Resistor [tolerance=±5% resistance=220 package=THT]
  R2 = Resistor [tolerance=±20% resistance=2.2k package=THT]
  R3 = Resistor [tolerance=±5% resistance=100 package=THT]

nets:
  N1: IR_transmitter.cathode, IR_receiver.anode, Arduino_Nano.GND, LED0.cathode
  N2: IR_transmitter.anode, R3.Pin_0
  N3: IR_receiver.cathode, Arduino_Nano.D7, R2.Pin_1
  N4: Arduino_Nano.5V, R2.Pin_0, R3.Pin_1
  N5: Arduino_Nano.D13/SCK, R1.Pin_1
  N6: LED0.anode, R1.Pin_0

notes:
  receiver
  transmitter
