# Fritzing sketch PIR_sensor (saved by Fritzing 0.9.4)
breadboards: 1

parts:
  PIR = PIR sensor
  Arduino_Nano = Arduino Nano (Rev3.0)
  LED1 = LED - 5mm [color="Red (633nm)" package="5 mm [THT]"]
  R1 = Resistor [tolerance=±5% resistance=220 package=THT]

nets:
  VDD: PIR.VDD, Arduino_Nano.5V
  N1: PIR.SIG, Arduino_Nano.D8
  GND: PIR.GND, Arduino_Nano.GND, LED1.cathode
  N2: Arduino_Nano.D3, R1.Pin_1
  N3: LED1.anode, R1.Pin_0
