# Fritzing sketch SRF05_sensor (saved by Fritzing 0.9.4)
breadboards: 1

parts:
  Arduino_Nano = Arduino Nano (Rev3.0)
  SRF-05 = HY-SRF05 Ultrasonic Rangefinder

nets (from the breadboard view):
  GND: Arduino_Nano.GND, SRF-05.GND
  N1: Arduino_Nano.D4, SRF-05.Trig, SRF-05.Echo
  5V: Arduino_Nano.5V, SRF-05.Vcc
